# Fritzing sketch PCF8574A-Expander-Board (saved by Fritzing 0.9.6b)
circuit board: 9.5292cm x 6.65356cm
stripboards: 1

parts:
  7_6 = female pin header, 2 pins [form="♀ (female)"]
  5_4 = female pin header, 2 pins [form="♀ (female)"]
  000 = PCF8574 [package="DIP16 [THT]"]
  100 = PCF8574 [package="DIP16 [THT]"]
  010 = PCF8574 [package="DIP16 [THT]"]
  110 = PCF8574 [package="DIP16 [THT]"]
  001 = PCF8574 [package="DIP16 [THT]"]
  101 = PCF8574 [package="DIP16 [THT]"]
  011 = PCF8574 [package="DIP16 [THT]"]
  111 = PCF8574 [package="DIP16 [THT]"]
  5_4_2 = female pin header, 2 pins [form="♀ (female)"]
  7_6_2 = female pin header, 2 pins [form="♀ (female)"]
  J11 = female pin header, 2 pins [form="♀ (female)"]
  J12 = female pin header, 2 pins [form="♀ (female)"]
  J13 = female pin header, 2 pins [form="♀ (female)"]
  J14 = female pin header, 2 pins [form="♀ (female)"]
  J15 = female pin header, 2 pins [form="♀ (female)"]
  J16 = female pin header, 2 pins [form="♀ (female)"]
  J17 = female pin header, 2 pins [form="♀ (female)"]
  2_3 = female pin header, 2 pins [form="♀ (female)"]
  |0_1 = female pin header, 2 pins [form="♀ (female)"]
  3_2 = female pin header, 2 pins [form="♀ (female)"]
  J33 = female pin header, 2 pins [form="♀ (female)"]
  0_1 = female pin header, 2 pins [form="♀ (female)"]
  J35 = female pin header, 2 pins [form="♀ (female)"]
  J36 = female pin header, 2 pins [form="♀ (female)"]
  J37 = female pin header, 2 pins [form="♀ (female)"]
  J38 = female pin header, 2 pins [form="♀ (female)"]
  J40 = female pin header, 2 pins [form="♀ (female)"]
  J42 = female pin header, 2 pins [form="♀ (female)"]
  J43 = female pin header, 2 pins [form="♀ (female)"]
  J44 = female pin header, 2 pins [form="♀ (female)"]
  J45 = female pin header, 2 pins [form="♀ (female)"]
  J46 = female pin header, 2 pins [form="♀ (female)"]
  J47 = female pin header, 2 pins [form="♀ (female)"]
  J48 = female pin header, 2 pins [form="♀ (female)"]
  J49 = female pin header, 2 pins [form="♀ (female)"]
  J50 = female pin header, 2 pins [form="♀ (female)"]
  J51 = female pin header, 2 pins [form="♀ (female)"]
  J53 = female pin header, 2 pins [form="♀ (female)"]
  J54 = female pin header, 2 pins [form="♀ (female)"]
  J55 = female pin header, 2 pins [form="♀ (female)"]
  J56 = female pin header, 2 pins [form="♀ (female)"]

nets:
  N1: 7_6.pin1, 000.P7
  N2: 7_6.pin2, 000.P6
  N3: 5_4.pin1, 000.P5
  N4: 5_4.pin2, 000.P4
  GND: 000.A0, 000.A1, 000.A2, 000.GND, 100.A1, 100.A2, 100.GND, 010.A0, 010.A2, 010.GND, 110.A2, 110.GND, 001.A0, 001.A1, 001.GND, 101.A1, 101.GND, 011.A0, 011.GND, 111.GND, J54.pin1, J54.pin2
  N5: 000.P0, 0_1.pin1
  N6: 000.P1, 0_1.pin2
  N7: 000.P2, 3_2.pin2
  N8: 000.P3, 3_2.pin1
  N9: 000.INT, 100.INT, 010.INT, 110.INT, 001.INT, 101.INT, 011.INT, 111.INT, J56.pin1
  N10: 000.SCL, 100.SCL, 010.SCL, 110.SCL, 001.SCL, 101.SCL, 011.SCL, 111.SCL, J56.pin2
  N11: 000.SDA, 100.SDA, 010.SDA, 110.SDA, 001.SDA, 101.SDA, 011.SDA, 111.SDA, J55.pin1
  VCC: 000.VCC, 100.A0, 100.VCC, 010.A1, 010.VCC, 110.A0, 110.A1, 110.VCC, 001.A2, 001.VCC, 101.A0, 101.A2, 101.VCC, 011.A1, 011.A2, 011.VCC, 111.A0, 111.A1, 111.A2, 111.VCC, J55.pin2
  N12: 100.P0, |0_1.pin1
  N13: 100.P1, |0_1.pin2
  N14: 100.P2, 2_3.pin1
  N15: 100.P3, 2_3.pin2
  N16: 100.P4, 5_4_2.pin2
  N17: 100.P5, 5_4_2.pin1
  N18: 100.P6, 7_6_2.pin2
  N19: 100.P7, 7_6_2.pin1
  N20: 010.P0, J35.pin1
  N21: 010.P1, J35.pin2
  N22: 010.P2, J33.pin1
  N23: 010.P3, J33.pin2
  N24: 010.P4, J11.pin2
  N25: 010.P5, J11.pin1
  N26: 010.P6, J12.pin2
  N27: 010.P7, J12.pin1
  N28: 110.P0, J37.pin1
  N29: 110.P1, J37.pin2
  N30: 110.P2, J36.pin1
  N31: 110.P3, J36.pin2
  N32: 110.P4, J13.pin2
  N33: 110.P5, J13.pin1
  N34: 110.P6, J14.pin2
  N35: 110.P7, J14.pin1
  N36: 001.P0, J53.pin2
  N37: 001.P1, J50.pin1
  N38: 001.P2, J50.pin2
  N39: 001.P3, J49.pin1
  N40: 001.P4, J51.pin1
  N41: 001.P5, J51.pin2
  N42: 001.P6, J49.pin2
  N43: 001.P7, J53.pin1
  N44: 101.P0, J44.pin2
  N45: 101.P1, J16.pin1
  N46: 101.P2, J16.pin2
  N47: 101.P3, J40.pin1
  N48: 101.P4, J40.pin2
  N49: 101.P5, J44.pin1
  N50: 101.P6, J45.pin2
  N51: 101.P7, J45.pin1
  N52: 011.P0, J48.pin1
  N53: 011.P1, J48.pin2
  N54: 011.P2, J38.pin1
  N55: 011.P3, J38.pin2
  N56: 011.P4, J47.pin2
  N57: 011.P5, J47.pin1
  N58: 011.P6, J43.pin2
  N59: 011.P7, J43.pin1
  N60: 111.P0, J46.pin1
  N61: 111.P1, J46.pin2
  N62: 111.P2, J17.pin1
  N63: 111.P3, J17.pin2
  N64: 111.P4, J15.pin2
  N65: 111.P5, J15.pin1
  N66: 111.P6, J42.pin2
  N67: 111.P7, J42.pin1

notes:
  GND
  GND
  VCC
  SDA
  SCL
  INT
